# Fritzing sketch AdfaberArduino2020 (saved by Fritzing 0.9.4)
breadboards: 1

parts:
  Part1 = Arduino Uno (Rev3)
  AM1 = AM2320 Humidity and Temperature Sensor [part_number="Adafruit #3721"]
  R1 = PHOTOCELL [package=photocell]  # not connected
  ZS-042_RTC1 = ZS-042 RTC Module  # not connected
  OLED1 = OLED 128x64 I2C Monochrome Display
  Part2 = IFR520 MOS module [package=THT]
  S1 = Pushbutton [package="[THT]"]  # not connected
  M1 = DC Motor
  BAT1 = Battery Holders [package=battery-aa]
  J1 = Piezo Speaker
  R2 = Resistor [tolerance=±5% resistance=10k package="2512 [SMD]"]
  R3 = Resistor [tolerance=±5% resistance=10k package="2512 [SMD]"]
  LED1 = RGB LED (com. anode, rbg) [package="5 mm [THT]"]  # not connected
  LED2 = RGB LED (com. anode, rbg) [package="5 mm [THT]"]  # not connected
  LED3 = RGB LED (com. anode, rbg) [package="5 mm [THT]"]  # not connected
  LED4 = RGB LED (com. anode, rbg) [package="5 mm [THT]"]  # not connected
  S2 = Pushbutton [package="[THT]"]  # not connected
  S3 = Pushbutton [package="[THT]"]  # not connected

nets:
  N1: Part1.A4/SDA, AM1.SDA, OLED1.SDA, R2.Pin_1
  N2: Part1.A5/SCL, AM1.SCL, OLED1.SCK, R3.Pin_0
  GND: Part1.GND, AM1.GND, OLED1.GND, Part2.pin3, J1.pin1
  N3: Part1.D2, Part2.pin1
  N4: Part1.D3_PWM, J1.pin2
  VDD: Part1.5V, AM1.VDD, OLED1.VDD, R2.Pin_0, R3.Pin_1
  N5: Part2.pin4, M1.pin_1
  N6: Part2.pin5, M1.pin_2
  N7: Part2.pin6, BAT1.+
  N8: Part2.pin7, BAT1.-

custom parts:
  AM2320 Humidity and Temperature Sensor: AM2320 I2C Humidity and Temperature Sensor
